# Fritzing sketch Schematic (saved by Fritzing 0.9.3b)
breadboards: 1

parts:
  Componente1 = STM32F407G-DISC1
  BT1 = Bluetooth HC-06u [package=THT]
  Componente2 = Passive Buzzer
  R2 = Photocell (LDR) [package=THT]
  Mod1 = KY-028 Digital Temperature Sensor Module [package="Breakout board"]
  U3 = HC-SR04 [chip_label=IC package="SIP (Single Inline) [THT]"]
  R3 = Resistor [tolerance=±2% resistance=330 package="0603 [SMD]"]
  R4 = Resistor [tolerance=±5% resistance=1k package="0603 [SMD]"]
  S1 = Pushbutton [package="[THT]"]
  J1 = Basic Servo
  S2 = Pushbutton [package="[THT]"]
  S3 = Pushbutton [package="[THT]"]
  LED2 = smd LED [color="Red (633nm)" package="0603 [SMD]"]
  S4 = Pushbutton [package="[THT]"]
  R5 = Resistor [tolerance=±5% resistance=10k package="0603 [SMD]"]
  R6 = Resistor [tolerance=±5% resistance=10k package="0603 [SMD]"]
  R7 = Resistor [tolerance=±5% resistance=10k package="0603 [SMD]"]
  R8 = Resistor [tolerance=±5% resistance=10k package="0603 [SMD]"]
  LED3 = smd LED [color="Red (633nm)" package="0603 [SMD]"]
  R9 = Resistor [tolerance=±5% resistance=330 package="0603 [SMD]"]
  R10 = Resistor [tolerance=±20% resistance=330 package="0603 [SMD]"]
  LED1 = smd LED [color="Red (633nm)" package="0603 [SMD]"]

nets:
  N1: Componente1.pin2, Componente1.pin86, R2.pin_0
  N2: Componente1.pin4, S1.Pin_1, S1.Pin_2, R5.Pin_0
  N3: Componente1.pin5, S3.Pin_1, S3.Pin_2, R6.Pin_0
  N4: Componente1.pin6, J1.pulse
  N5: Componente1.pin7, Mod1.A0
  GND: Componente1.pin12, Componente1.pin25, Componente1.pin26, Componente1.pin51, Componente1.pin75, Componente1.pin76, BT1.GND, Componente2.GND, Mod1.G, U3.GND, R4.Pin_1, J1.gnd, LED2.cathode, R5.Pin_1, R6.Pin_1, R7.Pin_1, R8.Pin_1, LED3.cathode, LED1.cathode
  N6: Componente1.pin14, U3.Echo
  N7: Componente1.pin30, S2.Pin_1, S2.Pin_2, R7.Pin_0
  N8: Componente1.pin32, R2.pin_1, R4.Pin_0
  N9: Componente1.pin33, S4.Pin_1, S4.Pin_2, R8.Pin_0
  N10: Componente1.pin36, Componente2.S
  VCC: Componente1.pin52, Componente1.pin77, BT1.VCC, Componente2.NC, Mod1.+, U3.Vcc, S1.Pin_3, S1.Pin_4, J1.vcc, S2.Pin_3, S2.Pin_4, S3.Pin_3, S3.Pin_4, S4.Pin_3, S4.Pin_4
  N11: Componente1.pin71, U3.Trig
  N12: Componente1.pin72, R10.Pin_0
  N13: Componente1.pin73, Componente1.pin74, BT1.RXD, R3.Pin_0
  N14: Componente1.pin98, R9.Pin_0
  N15: Componente1.pin99, BT1.TXD
  N16: R3.Pin_1, LED1.anode
  N17: LED2.anode, R9.Pin_1
  N18: LED3.anode, R10.Pin_1

notes:
  Luces ON/OFF
  Temperatura
  Puerta
  5 V
  3,3 V
  Alarma

custom parts:
  STM32F407G-DISC1: The STM32F4DISCOVERY Discovery kit allows users to easily develop applications with the STM32F407VG high-performance microcontroller with the Arm® Cortex®-M4 32-bit core. It includes everything required either for beginners or experienced users to get started quickly. Based on STM32F407VG, it includes an ST-LINK/V2-A embedded debug tool, one STMEMS digital accelerometer, one digital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
  Bluetooth HC-06u: Bluetooth HC-06 - face up, pins down 16.5mm x 37.5mm PCB
  KY-028 Digital Temperature Sensor Module: KY-028 Digital Temperature Sensor Module, used to measure changes in temperature.
  HC-SR04: HC-SR04 ultrasound distance sensor
